# Fritzing sketch Wiring (saved by Fritzing 0.9.3b)
circuit board: 15.5228cm x 7.40976cm
breadboards: 1

parts:
  J1 = Raspberry Pi Header 40pin [form="♂ (male)" package=THT]
  Part3 = Digital Temperature Sensor Breakout - TMP102
  LED1 = LED - 5mm [color="Blue (470nm)" package="5 mm [THT]"]
  Part2 = Arduino Uno (Rev3)
  AM1 = AM2302 Humidity and Temperature Sensor
  R1 = Resistor [tolerance=±5% resistance=220 package=THT]
  R2 = Resistor [tolerance=±5% resistance=220 package=THT]
  LED2 = LED - 5mm [color="Red (633nm)" package="5 mm [THT]"]
  Part1 = Ambient Light Sensor (TEMT6000 Breakout Board)

nets:
  3V3: J1.3v3, J1.3V3, Part3.V+
  N1: J1.GPIO2, Part3.SDA, Part2.A4/SDA
  N2: J1.GPIO3, Part3.SCL, Part2.A5/SCL
  GND: J1.GND, Part3.GND, LED1.cathode, Part2.GND, AM1.GND, LED2.cathode, Part1.GND
  N3: J1.GIPO26, AM1.DATA
  N4: J1.GIPO21, R2.Pin_1
  N5: J1.GIPO20, R1.Pin_1
  5V: J1.5V, AM1.VDD
  N6: LED1.anode, R1.Pin_0
  N7: Part2.A0, Part1.S
  5V_2: Part2.5V, Part1.VCC
  N8: R2.Pin_0, LED2.anode

custom parts:
  Raspberry Pi Header 40pin: Raspberry Pi 40 pin header - for creating your own shields.
